# Fritzing sketch breadboard_lte_meter (saved by Fritzing 0.9.0b)
breadboards: 1

parts:
  Raspberry_Pi1 = Raspberry Pi B rev2
  IC1 = IC, DIP package, 8 pins [chip_label=MCP4812]  # not connected
  C1 = Ceramic Capacitor [capacitance=100nF package="100 mil [THT, multilayer]"]
  LED1 = LED - 5mm [color="Red (633nm)" package="5 mm [THT]"]
  R1 = Resistor [tolerance=±5% resistance=460 package=THT]
  U1 = LM358 [package=dip08]  # not connected
  R2 = Trimmer Potentiometer [maximum_resistance=50kΩ package=THT]
  R3 = Resistor [tolerance=±5% resistance=10k package=THT]
  VCC1 = 4 x AAA Battery Mount
  VCC2 = 4 x AAA Battery Mount

nets:
  N1: Raspberry_Pi1.3V3, C1.0
  N2: Raspberry_Pi1.GPIO_25, R1.Pin_1
  N3: Raspberry_Pi1.GND, C1.1, LED1.cathode, R3.Pin_0, VCC2.-
  N4: LED1.anode, R1.Pin_0
  N5: R2.leg1, R3.Pin_1
  N6: VCC1.-, VCC2.+

notes:
  Connect 10V Panel Meter here
  Didn't found a power supply picture. Us a generic 12V DC supply for example.
